// Logisim project T20-Logism.circ as structural Verilog: 1 circuit, main circuit main
module main (
  input  in_1,
  input  in_2
);

  wire button_1_out, button_2_out, button_3_out, button_4_out, clock_1_out, decoder_1_out1, decoder_1_out2,
       decoder_1_out3, decoder_1_out4, decoder_1_out5, decoder_1_out6, decoder_1_out7, decoder_2_out1,
       decoder_2_out2, decoder_2_out3, decoder_2_out4, decoder_2_out5, decoder_2_out6, decoder_2_out7,
       or_1_out, or_2_out, or_3_out, or_4_out, or_5_out, or_6_out, or_7_out, or_8_out, or_9_out, or_10_out,
       or_11_out, or_12_out, or_13_out, or_14_out, or_15_out, or_16_out;
  wire [3:0] counter_1_q, counter_2_q;

  buf or_1 (or_1_out, decoder_1_out7);  // OR_Gate
  LED led_1 (.in(or_1_out));
  LED led_2 (.in(or_2_out));
  or or_2 (or_2_out, decoder_1_out7, decoder_1_out6);
  or or_3 (or_3_out, decoder_1_out7, decoder_1_out6, decoder_1_out5);
  LED led_3 (.in(or_3_out));
  or or_4 (or_4_out, decoder_1_out7, decoder_1_out6, decoder_1_out5, decoder_1_out4);
  LED led_4 (.in(or_4_out));
  LED led_5 (.in(or_5_out));
  or or_5 (or_5_out, decoder_1_out7, decoder_1_out6, decoder_1_out5, decoder_1_out4, decoder_1_out3);
  LED led_6 (.in(or_6_out));
  or or_6 (or_6_out, decoder_1_out7, decoder_1_out6, decoder_1_out5, decoder_1_out4, decoder_1_out3, decoder_1_out2);
  LED led_7 (.in(or_7_out));
  or or_7 (or_7_out, decoder_1_out7, decoder_1_out6, decoder_1_out5, decoder_1_out4, decoder_1_out3, decoder_1_out2, decoder_1_out1);
  LED led_8 (.in(decoder_1_out7));
  Button button_1 (.out(button_1_out));
  Hex_Digit_Display hex_digit_display_1 (.value(counter_1_q));  // open: dp
  Decoder #(.select(4)) decoder_1 (
    .out1(decoder_1_out1), .out2(decoder_1_out2), .out3(decoder_1_out3), .out4(decoder_1_out4),
    .out5(decoder_1_out5), .out6(decoder_1_out6), .out7(decoder_1_out7), .sel(counter_1_q), .en(in_1));  // open: out0, out8, out9, out10, out11, out12, out13, out14, out15
  Counter #(.width(4), .max('h7), .ongoal("stay")) counter_1 (
    .Q(counter_1_q), .clk(button_2_out), .clr(or_8_out));  // open: load, D, count, carry
  or or_8 (or_8_out, button_1_out, clock_1_out);
  Button button_2 (.out(button_2_out));
  Clock #(.lowDuration(100)) clock_1 (.out(clock_1_out));
  Button button_3 (.out(button_3_out));
  Counter #(.width(4), .max('h7), .ongoal("stay"), .trigger("falling")) counter_2 (
    .Q(counter_2_q), .clk(button_3_out), .clr(or_9_out));  // open: load, D, count, carry
  or or_9 (or_9_out, clock_1_out, button_4_out);
  Decoder #(.select(4)) decoder_2 (
    .out1(decoder_2_out1), .out2(decoder_2_out2), .out3(decoder_2_out3), .out4(decoder_2_out4),
    .out5(decoder_2_out5), .out6(decoder_2_out6), .out7(decoder_2_out7), .sel(counter_2_q), .en(in_2));  // open: out0, out8, out9, out10, out11, out12, out13, out14, out15
  Hex_Digit_Display hex_digit_display_2 (.value(counter_2_q));  // open: dp
  buf or_10 (or_10_out, decoder_2_out7);  // OR_Gate
  LED led_9 (.in(or_10_out));
  or or_11 (or_11_out, decoder_2_out7, decoder_2_out6);
  LED led_10 (.in(or_11_out));
  LED led_11 (.in(or_12_out));
  or or_12 (or_12_out, decoder_2_out7, decoder_2_out6, decoder_2_out5);
  or or_13 (or_13_out, decoder_2_out7, decoder_2_out6, decoder_2_out5, decoder_2_out4);
  LED led_12 (.in(or_13_out));
  or or_14 (or_14_out, decoder_2_out7, decoder_2_out6, decoder_2_out5, decoder_2_out4, decoder_2_out3);
  LED led_13 (.in(or_14_out));
  LED led_14 (.in(or_15_out));
  or or_15 (or_15_out, decoder_2_out7, decoder_2_out6, decoder_2_out5, decoder_2_out4, decoder_2_out3, decoder_2_out2);
  or or_16 (or_16_out, decoder_2_out7, decoder_2_out6, decoder_2_out5, decoder_2_out4, decoder_2_out3, decoder_2_out2, decoder_2_out1);
  LED led_15 (.in(or_16_out));
  LED led_16 (.in(decoder_2_out7));
  Button button_4 (.out(button_4_out));

  // Notes on the sheet:
  //   BIN - 2 is FULL
  //   FORCED EMPTY
  //   BIN - 2
  //   COUNT OF PLASTIC
  //   PLASTIC SENSOR
  //   INPUT
  //   INPUT TO SHAFT
  //   TIMED EMPTY
  //   NOTES :
  //   1. NUMBER OF LEDS GLOWING INDICATES HOW FILLED THE BIN IS
  //   2. PINK LEDS DEPICT THE BIN HAS REACHED MAXIMUM CAPACITY
  //   3. THE BINS / LEDS GET RESETED AFTER A FIXED TIME 
  //   4. FORCE EMPTY BUTTON RESETS THE LEDS AFTER BIN IS CLEARED
  //   NON-PLASTIC SENSOR
  //   COUNT OF NON - PLASTIC
  //   BIN - 1
  //   BIN - 1 is FULL
  //   FORCED EMPTY
endmodule
